# Fritzing sketch pm2.5_node (saved by Fritzing 0.9.3b)
circuit board: 8.46667cm x 5.64444cm

parts:
  U1 = NodeMCU V3.0
  LCD3 = LCD screen
  LCM1602_IIC3 = LCM1602 IIC [part_number="LCM1602 IIC" chip_label="LCM1602 IIC" package="DIP (Dual Inline) [THT]"]
  LED1 = LED - 5mm [color="Red (633nm)" package="5 mm [THT]"]
  LED2 = LED - 5mm [color="Green (560nm)" package="5 mm [THT]"]
  R1 = Resistor [tolerance=±5% resistance=330 package=THT]
  Dust_Sensor = mystery part, 6 pins [chip_label=?]
  Infrared = fc-51 [package=THT]
  buz1 = Piezo Buzzer
  Mod1 = gy-906

nets:
  Infrared: U1.D0, Infrared.pin1
  SCL: U1.D1, LCM1602_IIC3.SCL, Mod1.SCL
  SDA: U1.D2, LCM1602_IIC3.SDA, Mod1.SDA
  Buzzer: U1.D3, buz1.pin_1
  GND: U1.GND, LCM1602_IIC3.GND, R1.Pin_0, Dust_Sensor.pin2, Infrared.pin2, buz1.pin_2, Mod1.GND
  LED Green: U1.D5, LED2.anode
  LED Red: U1.D6, LED1.anode
  TXD: U1.D7, Dust_Sensor.pin5
  RXD: U1.D8, Dust_Sensor.pin4
  5V: U1.Vin, LCM1602_IIC3.VCC, Dust_Sensor.pin1, Infrared.pin3, Mod1.VIN
  VSS: LCD3.VSS, LCM1602_IIC3.VSS
  VDD: LCD3.VDD, LCM1602_IIC3.VDD
  N1: LCD3.V0, LCM1602_IIC3.V0
  N2: LCD3.RS, LCM1602_IIC3.RS
  N3: LCD3.R/W, LCM1602_IIC3.RW
  N4: LCD3.E, LCM1602_IIC3.E
  N5: LCD3.DB0, LCM1602_IIC3.D0
  N6: LCD3.DB1, LCM1602_IIC3.D1
  N7: LCD3.DB2, LCM1602_IIC3.D2
  N8: LCD3.DB3, LCM1602_IIC3.D3
  N9: LCD3.DB4, LCM1602_IIC3.D4
  N10: LCD3.DB5, LCM1602_IIC3.D5
  N11: LCD3.DB6, LCM1602_IIC3.D6
  N12: LCD3.DB7, LCM1602_IIC3.D7
  N13: LCD3.LED+, LCM1602_IIC3.A
  N14: LCM1602_IIC3.LED_A, LCM1602_IIC3.LED_B
  N15: LED1.cathode, LED2.cathode, R1.Pin_1

custom parts:
  NodeMCU V3.0: ESP8266 based NodeMCU
  LCM1602 IIC: I2C-Module to use a 1602 or 2004 LCD on with the wire.h libory Serial LCD Modul
  Piezo Buzzer: Part from https://www.nutsvolts.com/magazine/article/november2012_SmileysWorkshop modified to be .3 in spacing to match the adafruit buzzer 5V breadboard friendly part.
  gy-906: gy-906 Non-contact PIR I2C interface temperature sensor breakout board.
